// Logisim project ListaExercicios21-09.circ as structural Verilog: 2 circuits, main circuit main
module main (
  input  A,
  input  B,
  input  C,
  output out_4,
  output out_5,
  output out_6,
  output out_7,
  output out_8,
  output out_9
);

  wire and_1_out, and_2_out, nand_1_out, nand_2_out, nand_3_out, nand_4_out, nand_5_out, nand_6_out,
       nand_7_out, nand_8_out, nand_9_out, nand_10_out, nor_1_out, nor_2_out, nor_3_out, nor_4_out,
       nor_5_out, nor_6_out, nor_7_out, nor_8_out, nor_9_out, nor_11_out, nor_12_out, nor_13_out, not_1_out,
       or_1_out;

  not not_1 (not_1_out, or_1_out);
  or or_1 (or_1_out, A, B);
  nor nor_1 (nor_1_out, A, B);
  nor nor_2 (nor_2_out, C, C);
  nand nand_1 (nand_1_out, A, A);
  nand nand_2 (nand_2_out, B, B);
  and and_1 (and_1_out, A, ~B, C);  // AND_Gate
  and and_2 (and_2_out, A, B);
  nand nand_3 (nand_3_out, B, B);
  nand nand_4 (nand_4_out, A, B);
  nor nor_3 (nor_3_out, A, A);
  nor nor_4 (nor_4_out, B, B);
  nor nor_5 (nor_5_out, C, C);
  nor nor_6 (nor_6_out, nor_4_out, nor_4_out);
  nor nor_7 (nor_7_out, A, A);
  nor nor_8 (nor_8_out, B, B);
  and and_3 (out_4, not_1_out, C);
  nor nor_9 (nor_9_out, nor_1_out, nor_1_out);
  nand nand_5 (nand_5_out, nand_1_out, nand_2_out);
  or or_2 (out_7, and_1_out, and_2_out);
  nand nand_6 (nand_6_out, A, nand_3_out, C);
  nand nand_7 (nand_7_out, nand_4_out, nand_4_out);
  nor nor_10 (out_5, nor_9_out, nor_2_out);
  nand nand_8 (nand_8_out, nand_5_out, nand_5_out);
  nand nand_9 (nand_9_out, nand_7_out, nand_7_out);
  nor nor_11 (nor_11_out, nor_3_out, nor_6_out, nor_5_out);
  nor nor_12 (nor_12_out, nor_7_out, nor_8_out);
  nand nand_10 (nand_10_out, nand_8_out, C);
  nand nand_11 (out_8, nand_6_out, nand_9_out);
  nor nor_13 (nor_13_out, nor_11_out, nor_12_out);
  nand nand_12 (out_6, nand_10_out, nand_10_out);
  nor nor_14 (out_9, nor_13_out, nor_13_out);

  // Notes on the sheet:
  //   B) X = (A+B)'C
  //   B) Somente com NOR
  //   B) Somente com NAND
  //   C) X = AB'C + AB
  //   C) Somente com NAND
  //   C) Somente com NOR
endmodule

module questao_D__questao_E (
  input  C,
  input  A,
  input  B,
  output out_4,
  output out_5,
  output out_6,
  output out_7,
  output out_8,
  output out_9
);

  wire and_1_out, nand_1_out, nand_2_out, nand_3_out, nand_4_out, nand_5_out, nand_6_out, nand_7_out,
       nand_8_out, nand_9_out, nand_10_out, nand_11_out, nor_1_out, nor_2_out, nor_3_out, nor_4_out,
       nor_5_out, nor_6_out, nor_7_out, nor_8_out, nor_9_out, nor_11_out, or_1_out, or_2_out, or_3_out,
       or_4_out;

  and and_1 (and_1_out, B, C);
  or or_1 (or_1_out, ~B, ~C);  // OR_Gate
  nand nand_1 (nand_1_out, A, A);
  nand nand_2 (nand_2_out, B, C);
  or or_2 (or_2_out, A, B);
  or or_3 (or_3_out, ~A, B);  // OR_Gate
  nand nand_3 (nand_3_out, A, A);
  nand nand_4 (nand_4_out, B, B);
  nand nand_5 (nand_5_out, B, B);
  nor nor_1 (nor_1_out, A, B);
  nor nor_2 (nor_2_out, A, A);
  nor nor_3 (nor_3_out, B, B);
  nor nor_4 (nor_4_out, C, C);
  nor nor_5 (nor_5_out, B, B);
  nor nor_6 (nor_6_out, C, C);
  and and_2 (out_4, or_2_out, or_3_out);
  nand nand_6 (nand_6_out, nand_3_out, nand_4_out);
  nand nand_7 (nand_7_out, A, nand_5_out);
  nor nor_7 (nor_7_out, nor_2_out, B);
  or or_4 (or_4_out, A, and_1_out);
  nand nand_8 (nand_8_out, B, C);
  nor nor_8 (nor_8_out, nor_3_out, nor_4_out);
  nor nor_9 (nor_9_out, nor_5_out, nor_6_out);
  nand nand_9 (nand_9_out, nand_1_out, nand_2_out);
  nand nand_10 (nand_10_out, nand_6_out, nand_7_out);
  nor nor_10 (out_6, nor_1_out, nor_7_out);
  and and_3 (out_7, or_4_out, or_1_out);
  nor nor_11 (nor_11_out, A, nor_8_out);
  nand nand_11 (nand_11_out, nand_9_out, nand_8_out);
  nand nand_12 (out_5, nand_10_out, nand_10_out);
  nand nand_13 (out_8, nand_11_out, nand_11_out);
  nor nor_12 (out_9, nor_11_out, nor_9_out);

  // Notes on the sheet:
  //   D) (A+B)(A'+B)
  //   D) Somente com NAND
  //   D) Somente com NOR
  //   E) (A+BC)(B'+C')
  //   E)  Somente com NAND
  //   E)  Somente com NOR
endmodule
