// Logisim project aula_1409.circ as structural Verilog: 1 circuit, main circuit main
module main (
  input  A,
  input  B,
  output out_3,
  output out_4,
  output out_5,
  output out_6
);

  wire nand_1_out, nand_2_out, nor_2_out, nor_4_out, nor_5_out;

  nand nand_1 (nand_1_out, A, A);
  nand nand_2 (nand_2_out, B, B);
  nor nor_1 (out_4, A, A);
  nor nor_2 (nor_2_out, A, B);
  nor nor_3 (out_6, nor_2_out, nor_2_out);
  nand nand_3 (out_3, nand_1_out, nand_2_out);
  nor nor_4 (nor_4_out, A, A);
  nor nor_5 (nor_5_out, A, A);
  nor nor_6 (out_5, nor_4_out, nor_5_out);
endmodule
