// Logisim project tf_parte_2.circ as structural Verilog: 15 circuits, main circuit main
module latch_D (
  input  in_1,
  input  in_2,
  output out_3
);

  wire and_1_out, and_2_out, nor_1_out, not_1_out;

  not not_1 (not_1_out, in_1);
  and and_1 (and_1_out, in_1, in_2);
  and and_2 (and_2_out, in_2, not_1_out);
  nor nor_1 (nor_1_out, and_1_out, out_3);
  nor nor_2 (out_3, nor_1_out, and_2_out);
endmodule

module flip_flop_D (
  input  in_1,
  input  in_2,
  output out_3
);

  wire latch_d_1_out_3, not_1_out;

  latch_D latch_d_1 (.in_1(in_1), .out_3(latch_d_1_out_3), .in_2(not_1_out));
  not not_1 (not_1_out, in_2);
  latch_D latch_d_2 (.in_1(latch_d_1_out_3), .out_3(out_3), .in_2(in_2));
endmodule

module parte_1 (
  input  [2:0] Sel_read_a,
  input  [2:0] Sel_read_b,
  input  Write,
  input  [2:0] Sel_Write,
  input  [7:0] Data_in,
  input  Clock,
  output [7:0] Dout_a,
  output [7:0] Dout_b
);

  wire [7:0] registrador_8bits_1_r0, registrador_8bits_1_r1, registrador_8bits_1_r2, registrador_8bits_1_r3,
       registrador_8bits_1_r4, registrador_8bits_1_r5, registrador_8bits_1_r6, registrador_8bits_1_r7;

  registrador_8bits registrador_8bits_1 (
    .Write(Write), .Seletor(Sel_Write), .DATA(Data_in), .R0(registrador_8bits_1_r0),
    .R1(registrador_8bits_1_r1), .R2(registrador_8bits_1_r2), .R3(registrador_8bits_1_r3),
    .R4(registrador_8bits_1_r4), .R5(registrador_8bits_1_r5), .R6(registrador_8bits_1_r6),
    .R7(registrador_8bits_1_r7), .Clk(Clock));
  seleciona_reg seleciona_reg_1 (
    .Sel(Sel_read_a), .D0(registrador_8bits_1_r0), .D1(registrador_8bits_1_r1), .D2(registrador_8bits_1_r2),
    .D3(registrador_8bits_1_r3), .D4(registrador_8bits_1_r4), .D5(registrador_8bits_1_r5),
    .D6(registrador_8bits_1_r6), .D7(registrador_8bits_1_r7), .Data_out(Dout_a));
  seleciona_reg seleciona_reg_2 (
    .Sel(Sel_read_b), .D0(registrador_8bits_1_r0), .D1(registrador_8bits_1_r1), .D2(registrador_8bits_1_r2),
    .D3(registrador_8bits_1_r3), .D4(registrador_8bits_1_r4), .D5(registrador_8bits_1_r5),
    .D6(registrador_8bits_1_r6), .D7(registrador_8bits_1_r7), .Data_out(Dout_b));

  // Notes on the sheet:
  //   Banco de Registradores de 8 bits que visualiza a saída de dois registradores
endmodule

module flip_flop_D_8bits (
  input  [7:0] in_1,
  input  in_2,
  output [7:0] out_3
);

  flip_flop_D flip_flop_d_1 (.in_1(in_1[7]), .in_2(in_2), .out_3(out_3[7]));
  flip_flop_D flip_flop_d_2 (.in_1(in_1[6]), .in_2(in_2), .out_3(out_3[6]));
  flip_flop_D flip_flop_d_3 (.in_1(in_1[5]), .in_2(in_2), .out_3(out_3[5]));
  flip_flop_D flip_flop_d_4 (.in_1(in_1[4]), .in_2(in_2), .out_3(out_3[4]));
  flip_flop_D flip_flop_d_5 (.in_1(in_1[3]), .in_2(in_2), .out_3(out_3[3]));
  flip_flop_D flip_flop_d_6 (.in_1(in_1[1]), .in_2(in_2), .out_3(out_3[1]));
  flip_flop_D flip_flop_d_7 (.in_1(in_1[2]), .in_2(in_2), .out_3(out_3[2]));
  flip_flop_D flip_flop_d_8 (.in_1(in_1[0]), .in_2(in_2), .out_3(out_3[0]));

  // Notes on the sheet:
  //   FLIP FLOP D DE 8 BITS EM PARALELO
endmodule

module registrador_enable (
  input  [7:0] D,
  input  En,
  input  in_3,
  output [7:0] R
);

  wire [7:0] mux_8x1_1_q;

  MUX_8x1 mux_8x1_1 (.A(R), .Sel(En), .B(D), .Q(mux_8x1_1_q));
  flip_flop_D_8bits flip_flop_d_8bits_1 (.in_1(mux_8x1_1_q), .out_3(R), .in_2(in_3));
endmodule

module MUX_2x1 (
  input  A,
  input  Sel,
  input  B,
  output out_4
);

  wire and_1_out, and_2_out, not_1_out;

  not not_1 (not_1_out, Sel);
  and and_1 (and_1_out, A, not_1_out);
  and and_2 (and_2_out, Sel, B);
  or or_1 (out_4, and_1_out, and_2_out);
endmodule

module MUX_8x1 (
  input  [7:0] A,
  input  Sel,
  input  [7:0] B,
  output [7:0] Q
);

  MUX_2x1 _7 (.A(A[7]), .Sel(Sel), .B(B[7]), .out_4(Q[7]));
  MUX_2x1 _6 (.A(A[6]), .Sel(Sel), .B(B[6]), .out_4(Q[6]));
  MUX_2x1 _5 (.A(A[5]), .Sel(Sel), .B(B[5]), .out_4(Q[5]));
  MUX_2x1 _4 (.A(A[4]), .Sel(Sel), .B(B[4]), .out_4(Q[4]));
  MUX_2x1 _3 (.A(A[3]), .Sel(Sel), .B(B[3]), .out_4(Q[3]));
  MUX_2x1 _2 (.A(A[2]), .Sel(Sel), .B(B[2]), .out_4(Q[2]));
  MUX_2x1 _1 (.A(A[1]), .Sel(Sel), .B(B[1]), .out_4(Q[1]));
  MUX_2x1 _0 (.A(A[0]), .Sel(Sel), .B(B[0]), .out_4(Q[0]));
endmodule

module registrador_8bits (
  input  Write,
  input  [2:0] Seletor,
  input  [7:0] DATA,
  input  Clk,
  output [7:0] R0,
  output [7:0] R1,
  output [7:0] R2,
  output [7:0] R3,
  output [7:0] R4,
  output [7:0] R5,
  output [7:0] R6,
  output [7:0] R7
);

  wire seletor_write_1_q0, seletor_write_1_q1, seletor_write_1_q2, seletor_write_1_q3, seletor_write_1_q4,
       seletor_write_1_q5, seletor_write_1_q6, seletor_write_1_q7;

  seletor_write seletor_write_1 (
    .Sel(Seletor), .Q0(seletor_write_1_q0), .Q1(seletor_write_1_q1), .Q2(seletor_write_1_q2),
    .Q3(seletor_write_1_q3), .Q4(seletor_write_1_q4), .Q5(seletor_write_1_q5), .Q6(seletor_write_1_q6),
    .Q7(seletor_write_1_q7), .Write(Write));
  registrador_enable _7 (.D(DATA), .En(seletor_write_1_q7), .R(R7), .in_3(Clk));
  registrador_enable _6 (.D(DATA), .En(seletor_write_1_q6), .R(R6), .in_3(Clk));
  registrador_enable _5 (.D(DATA), .En(seletor_write_1_q5), .R(R5), .in_3(Clk));
  registrador_enable _4 (.D(DATA), .En(seletor_write_1_q4), .R(R4), .in_3(Clk));
  registrador_enable _3 (.D(DATA), .En(seletor_write_1_q3), .R(R3), .in_3(Clk));
  registrador_enable _2 (.D(DATA), .En(seletor_write_1_q2), .R(R2), .in_3(Clk));
  registrador_enable _1 (.D(DATA), .En(seletor_write_1_q1), .R(R1), .in_3(Clk));
  registrador_enable _0 (.D(DATA), .En(seletor_write_1_q0), .R(R0), .in_3(Clk));
endmodule

module seletor_write (
  input  [2:0] Sel,
  input  Write,
  output Q0,
  output Q1,
  output Q2,
  output Q3,
  output Q4,
  output Q5,
  output Q6,
  output Q7
);

  and and_1 (Q0, Write, ~Sel[2], ~Sel[1], ~Sel[0]);  // AND_Gate
  and and_2 (Q1, Write, ~Sel[2], ~Sel[1], Sel[0]);  // AND_Gate
  and and_3 (Q2, Write, ~Sel[2], Sel[1], ~Sel[0]);  // AND_Gate
  and and_4 (Q3, Write, ~Sel[2], Sel[1], Sel[0]);  // AND_Gate
  and and_5 (Q4, Write, Sel[2], ~Sel[1], ~Sel[0]);  // AND_Gate
  and and_6 (Q5, Write, Sel[2], ~Sel[1], Sel[0]);  // AND_Gate
  and and_7 (Q6, Write, Sel[2], Sel[1], ~Sel[0]);  // AND_Gate
  and and_8 (Q7, Write, Sel[2], Sel[1], Sel[0]);

  // Notes on the sheet:
  //   SELETOR
endmodule

module seleciona_reg (
  input  [2:0] Sel,
  input  [7:0] D0,
  input  [7:0] D1,
  input  [7:0] D2,
  input  [7:0] D3,
  input  [7:0] D4,
  input  [7:0] D5,
  input  [7:0] D6,
  input  [7:0] D7,
  output [7:0] Data_out
);

  wire [7:0] mux_8x1_1_q, mux_8x1_2_q, mux_8x1_3_q, mux_8x1_4_q, mux_8x1_5_q, mux_8x1_6_q;

  MUX_8x1 mux_8x1_1 (.A(D0), .Sel(Sel[0]), .B(D1), .Q(mux_8x1_1_q));
  MUX_8x1 mux_8x1_2 (.A(D2), .Sel(Sel[0]), .B(D3), .Q(mux_8x1_2_q));
  MUX_8x1 mux_8x1_3 (.A(D4), .Sel(Sel[0]), .B(D5), .Q(mux_8x1_3_q));
  MUX_8x1 mux_8x1_4 (.A(D6), .Sel(Sel[0]), .B(D7), .Q(mux_8x1_4_q));
  MUX_8x1 mux_8x1_5 (.A(mux_8x1_1_q), .Sel(Sel[1]), .B(mux_8x1_2_q), .Q(mux_8x1_5_q));
  MUX_8x1 mux_8x1_6 (.A(mux_8x1_3_q), .Sel(Sel[1]), .B(mux_8x1_4_q), .Q(mux_8x1_6_q));
  MUX_8x1 mux_8x1_7 (.A(mux_8x1_5_q), .Sel(Sel[2]), .B(mux_8x1_6_q), .Q(Data_out));
endmodule

module soma_completo (
  input  Ant,
  input  A,
  input  B,
  output SF,
  output SV
);

  wire and_1_out, and_2_out, and_3_out, and_4_out, and_5_out, and_6_out, and_7_out;

  and and_1 (and_1_out, ~Ant, ~A, B);  // AND_Gate
  and and_2 (and_2_out, ~Ant, A, ~B);  // AND_Gate
  and and_3 (and_3_out, Ant, ~A, ~B);  // AND_Gate
  and and_4 (and_4_out, Ant, A, B);
  and and_5 (and_5_out, A, B);
  and and_6 (and_6_out, Ant, A);
  and and_7 (and_7_out, Ant, B);
  or or_1 (SF, and_1_out, and_2_out, and_3_out, and_4_out);
  or or_2 (SV, and_5_out, and_6_out, and_7_out);

  // Notes on the sheet:
  //   Circuito Somador completo
endmodule

module soma_subtrator (
  input  [7:0] B,
  input  [7:0] A,
  input  C,
  output [7:0] S
);

  wire soma_completo_2_sv, soma_completo_3_sv, soma_completo_4_sv, soma_completo_5_sv, soma_completo_6_sv,
       soma_completo_7_sv, soma_completo_8_sv, xor_1_out, xor_2_out, xor_3_out, xor_4_out, xor_5_out,
       xor_6_out, xor_7_out, xor_8_out;

  xor xor_1 (xor_1_out, C, B[7]);
  soma_completo soma_completo_1 (.SF(S[7]), .Ant(soma_completo_2_sv), .A(A[7]), .B(xor_1_out));  // open: SV
  soma_completo soma_completo_2 (.SF(S[6]), .SV(soma_completo_2_sv), .Ant(soma_completo_3_sv), .A(A[6]), .B(xor_2_out));
  xor xor_2 (xor_2_out, C, B[6]);
  xor xor_3 (xor_3_out, C, B[5]);
  soma_completo soma_completo_3 (.SF(S[5]), .SV(soma_completo_3_sv), .Ant(soma_completo_4_sv), .A(A[5]), .B(xor_3_out));
  soma_completo soma_completo_4 (.SF(S[4]), .SV(soma_completo_4_sv), .Ant(soma_completo_5_sv), .A(A[4]), .B(xor_4_out));
  xor xor_4 (xor_4_out, C, B[4]);
  xor xor_5 (xor_5_out, C, B[3]);
  soma_completo soma_completo_5 (.SF(S[3]), .SV(soma_completo_5_sv), .Ant(soma_completo_6_sv), .A(A[3]), .B(xor_5_out));
  soma_completo soma_completo_6 (.SF(S[2]), .SV(soma_completo_6_sv), .Ant(soma_completo_7_sv), .A(A[2]), .B(xor_6_out));
  xor xor_6 (xor_6_out, C, B[2]);
  xor xor_7 (xor_7_out, C, B[1]);
  soma_completo soma_completo_7 (.SF(S[1]), .SV(soma_completo_7_sv), .Ant(soma_completo_8_sv), .A(A[1]), .B(xor_7_out));
  soma_completo soma_completo_8 (.SF(S[0]), .SV(soma_completo_8_sv), .Ant(C), .A(A[0]), .B(xor_8_out));
  xor xor_8 (xor_8_out, C, B[0]);
endmodule

module ULA (
  input  [7:0] A,
  input  [7:0] B,
  input  [1:0] Sel,
  output [7:0] ula_out
);

  wire [7:0] and_1_out, mux_8x1_1_q, mux_8x1_2_q, or_1_out, soma_subtrator_1_s;

  assign and_1_out = A & B;  // AND_Gate and_1, 8 bits wide
  assign or_1_out = A | B;  // OR_Gate or_1, 8 bits wide
  soma_subtrator soma_subtrator_1 (.B(B), .A(A), .C(Sel[0]), .S(soma_subtrator_1_s));
  MUX_8x1 mux_8x1_1 (.A(and_1_out), .Sel(Sel[0]), .B(or_1_out), .Q(mux_8x1_1_q));
  MUX_8x1 mux_8x1_2 (.A(soma_subtrator_1_s), .Sel(Sel[1]), .B(soma_subtrator_1_s), .Q(mux_8x1_2_q));
  MUX_8x1 mux_8x1_3 (.A(mux_8x1_1_q), .Sel(Sel[1]), .B(mux_8x1_2_q), .Q(ula_out));
endmodule

module sel_som_sub (
  input  [7:0] A,
  input  [7:0] B,
  input  Sel
);

  soma_subtrator soma_subtrator_1 (.B(A), .A(B));  // open: C, S
endmodule

module main (
  input  [1:0] SEL_OPERATION,
  input  [2:0] SEL_READ_A,
  input  [2:0] SEL_READ_B,
  input  WRITE,
  input  [2:0] SEL_WRITE,
  input  [7:0] DATA_IN,
  input  SEL_DIN,
  output [7:0] ULA_OUT
);

  wire CLOCK_out;
  wire [7:0] mux_8x1_1_q, parte_1_1_dout_a, parte_1_1_dout_b;

  MUX_8x1 mux_8x1_1 (.A(DATA_IN), .Sel(SEL_DIN), .B(ULA_OUT), .Q(mux_8x1_1_q));
  Clock CLOCK (.out(CLOCK_out));
  parte_1 parte_1_1 (
    .Sel_read_a(SEL_READ_A), .Sel_read_b(SEL_READ_B), .Write(WRITE), .Sel_Write(SEL_WRITE),
    .Data_in(mux_8x1_1_q), .Dout_a(parte_1_1_dout_a), .Dout_b(parte_1_1_dout_b), .Clock(CLOCK_out));
  ULA ula_1 (.A(parte_1_1_dout_a), .B(parte_1_1_dout_b), .Sel(SEL_OPERATION), .ula_out(ULA_OUT));

  // Notes on the sheet:
  //   ULA COM SALVAMENTO EM UM REGISTRADOR DE 8 BITS
  //   Alunos: Matheus Baron Lauritzen, Gustavo Baron Lauritzen e Gabriel Bósio
endmodule
