// Logisim project exercicios_NAND_NOR.circ as structural Verilog
module QUESTAO_A (
  input  A,
  input  B,
  input  C,
  output X,
  output X_2,
  output X_3
);

  wire and_1_out, nand_1_out, nand_2_out, nand_3_out, nand_4_out, nand_5_out, nand_6_out, nand_7_out,
       nor_1_out, nor_2_out, nor_3_out, nor_4_out, nor_5_out, nor_6_out, or_1_out;

  or or_1 (or_1_out, A, B);
  nor nor_1 (nor_1_out, A, B);
  nand nand_1 (nand_1_out, A, A);
  nand nand_2 (nand_2_out, B, B);
  and and_1 (and_1_out, or_1_out, C);
  nor nor_2 (nor_2_out, nor_1_out, nor_1_out);
  nand nand_3 (nand_3_out, nand_1_out, nand_2_out);
  or or_2 (X, and_1_out, B);
  nor nor_3 (nor_3_out, nor_2_out, nor_2_out);
  nor nor_4 (nor_4_out, C, C);
  nand nand_4 (nand_4_out, nand_3_out, C);
  nor nor_5 (nor_5_out, nor_3_out, nor_4_out);
  nand nand_5 (nand_5_out, nand_4_out, nand_4_out);
  nor nor_6 (nor_6_out, nor_5_out, B);
  nand nand_6 (nand_6_out, nand_5_out, nand_5_out);
  nand nand_7 (nand_7_out, B, B);
  nor nor_7 (X_2, nor_6_out, nor_6_out);
  nand nand_8 (X_3, nand_6_out, nand_7_out);

  // Notes on the sheet:
  //   x  = (A+B)C + B
  //   A) SOMENTE NOR
  //   A) SOMENTE NAND
endmodule

module QUESTAO_B (
  input  A,
  input  B,
  input  C,
  output X,
  output X_2,
  output X_3
);

  wire nand_1_out, nand_2_out, nand_3_out, nand_4_out, nand_5_out, nor_1_out, nor_2_out, nor_4_out,
       not_1_out, or_1_out;

  or or_1 (or_1_out, A, B);
  nor nor_1 (nor_1_out, A, B);
  nand nand_1 (nand_1_out, A, A);
  nand nand_2 (nand_2_out, B, B);
  not not_1 (not_1_out, or_1_out);
  and and_1 (X, not_1_out, C);
  nand nand_3 (nand_3_out, nand_1_out, nand_2_out);
  nor nor_2 (nor_2_out, nor_1_out, nor_1_out);
  nor nor_3 (X_2, nor_2_out, nor_4_out);
  nor nor_4 (nor_4_out, C, C);
  nand nand_4 (nand_4_out, nand_3_out, nand_3_out);
  nand nand_5 (nand_5_out, nand_4_out, C);
  nand nand_6 (X_3, nand_5_out, nand_5_out);

  // Notes on the sheet:
  //   x  = (A+B)'C
  //   SOMENTE NOR
  //   SOMENTE NAND
endmodule

module QUESTAO_C (
  input  A,
  input  B,
  input  C,
  output X,
  output X_2,
  output X_3,
  output X_4
);

  wire and_1_out, and_2_out, and_3_out, and_4_out, and_5_out, nand_1_out, nand_2_out, nand_3_out, nand_4_out,
       nand_5_out, nand_6_out, nand_7_out, nand_8_out, nand_10_out, nor_1_out, nor_2_out, nor_3_out,
       nor_4_out, nor_5_out, nor_6_out, nor_7_out, nor_8_out, nor_9_out, nor_10_out, nor_11_out, not_1_out,
       not_2_out;

  not not_1 (not_1_out, B);
  not not_2 (not_2_out, B);
  nor nor_1 (nor_1_out, B, B);
  nand nand_1 (nand_1_out, B, B);
  and and_1 (and_1_out, A, not_1_out, C);
  or or_1 (X, and_1_out, and_2_out);
  and and_2 (and_2_out, A, B);
  and and_3 (and_3_out, A, not_2_out);
  and and_4 (and_4_out, and_3_out, C);
  nor nor_2 (nor_2_out, A, A);
  nor nor_3 (nor_3_out, nor_1_out, nor_1_out);
  nor nor_4 (nor_4_out, A, A);
  nor nor_5 (nor_5_out, B, B);
  nand nand_2 (nand_2_out, A, nand_1_out);
  nand nand_3 (nand_3_out, A, B);
  and and_5 (and_5_out, A, B);
  nor nor_6 (nor_6_out, nor_2_out, nor_3_out);
  nor nor_7 (nor_7_out, nor_4_out, nor_5_out);
  nand nand_4 (nand_4_out, nand_2_out, nand_2_out);
  nand nand_5 (nand_5_out, nand_3_out, nand_3_out);
  or or_2 (X_2, and_4_out, and_5_out);
  nor nor_8 (nor_8_out, nor_6_out, nor_6_out);
  nor nor_9 (nor_9_out, C, C);
  nand nand_6 (nand_6_out, nand_4_out, C);
  nor nor_10 (nor_10_out, nor_8_out, nor_9_out);
  nand nand_7 (nand_7_out, nand_6_out, nand_6_out);
  nor nor_11 (nor_11_out, nor_10_out, nor_7_out);
  nand nand_8 (nand_8_out, nand_7_out, nand_7_out);
  nand nand_9 (X_4, nand_8_out, nand_10_out);
  nand nand_10 (nand_10_out, nand_5_out, nand_5_out);
  nor nor_12 (X_3, nor_11_out, nor_11_out);

  // Notes on the sheet:
  //   x  = AB'C+AB
  //   SOMENTE NOR
  //   SOMENTE NAND
  //   x  = (AB')C+AB
endmodule

module QUESTAO_D (
  input  A,
  input  B,
  input  C,
  output X,
  output X_2,
  output X_3
);

  wire nand_1_out, nand_2_out, nand_3_out, nand_4_out, nand_5_out, nand_6_out, nand_7_out, nand_9_out,
       nor_1_out, nor_2_out, nor_3_out, nor_4_out, nor_5_out, nor_6_out, nor_7_out, not_1_out, or_1_out,
       or_2_out;

  not not_1 (not_1_out, A);
  nor nor_1 (nor_1_out, A, A);
  nand nand_1 (nand_1_out, A, A);
  or or_1 (or_1_out, A, B);
  and and_1 (X, or_1_out, or_2_out);
  or or_2 (or_2_out, not_1_out, B);
  nor nor_2 (nor_2_out, A, B);
  nor nor_3 (nor_3_out, nor_1_out, B);
  nand nand_2 (nand_2_out, A, A);
  nand nand_3 (nand_3_out, B, B);
  nand nand_4 (nand_4_out, nand_1_out, nand_1_out);
  nand nand_5 (nand_5_out, B, B);
  nor nor_4 (nor_4_out, nor_2_out, nor_2_out);
  nor nor_5 (nor_5_out, nor_3_out, nor_3_out);
  nand nand_6 (nand_6_out, nand_2_out, nand_3_out);
  nand nand_7 (nand_7_out, nand_4_out, nand_5_out);
  nor nor_6 (nor_6_out, nor_4_out, nor_4_out);
  nor nor_7 (nor_7_out, nor_5_out, nor_5_out);
  nand nand_8 (X_3, nand_9_out, nand_9_out);
  nand nand_9 (nand_9_out, nand_6_out, nand_7_out);
  nor nor_8 (X_2, nor_6_out, nor_7_out);

  // Notes on the sheet:
  //   x  = (A+B)(A'+B)
  //   SOMENTE NOR
  //   SOMENTE NAND
endmodule

module QUESTAO_E (
  input  A,
  input  B,
  input  C,
  output X,
  output X_2,
  output X_3
);

  wire and_1_out, nand_1_out, nand_2_out, nand_3_out, nand_4_out, nand_5_out, nand_6_out, nand_7_out,
       nand_8_out, nand_9_out, nand_10_out, nand_11_out, nor_1_out, nor_2_out, nor_3_out, nor_4_out,
       nor_5_out, nor_6_out, nor_7_out, nor_8_out, nor_9_out, nor_10_out, nor_11_out, not_1_out, not_2_out,
       or_1_out, or_2_out;

  and and_1 (and_1_out, B, C);
  not not_1 (not_1_out, B);
  not not_2 (not_2_out, C);
  nor nor_1 (nor_1_out, B, B);
  nor nor_2 (nor_2_out, nor_1_out, nor_3_out);
  nor nor_3 (nor_3_out, C, C);
  nor nor_4 (nor_4_out, B, B);
  nor nor_5 (nor_5_out, nor_4_out, nor_6_out);
  nor nor_6 (nor_6_out, C, C);
  nand nand_1 (nand_1_out, B, C);
  nand nand_2 (nand_2_out, nand_1_out, nand_1_out);
  nand nand_3 (nand_3_out, B, B);
  nand nand_4 (nand_4_out, nand_3_out, nand_3_out);
  nand nand_5 (nand_5_out, C, C);
  nand nand_6 (nand_6_out, nand_5_out, nand_5_out);
  or or_1 (or_1_out, A, and_1_out);
  and and_2 (X, or_1_out, or_2_out);
  or or_2 (or_2_out, not_1_out, not_2_out);
  nor nor_7 (nor_7_out, nor_5_out, nor_5_out);
  nand nand_7 (nand_7_out, A, A);
  nand nand_8 (nand_8_out, nand_2_out, nand_2_out);
  nand nand_9 (nand_9_out, nand_4_out, nand_6_out);
  nor nor_8 (nor_8_out, A, nor_2_out);
  nor nor_9 (nor_9_out, nor_8_out, nor_8_out);
  nand nand_10 (nand_10_out, nand_7_out, nand_8_out);
  nor nor_10 (nor_10_out, nor_9_out, nor_9_out);
  nor nor_11 (nor_11_out, nor_7_out, nor_7_out);
  nand nand_11 (nand_11_out, nand_10_out, nand_9_out);
  nand nand_12 (X_3, nand_11_out, nand_11_out);
  nor nor_12 (X_2, nor_10_out, nor_11_out);

  // Notes on the sheet:
  //   x  = (A+BC)(B'+C')
  //   SOMENTE NOR
  //   SOMENTE NAND
endmodule
