// Logisim project latch_flip_flop.circ as structural Verilog: 9 circuits, main circuit main
module main (
  input  [3:0] A,
  input  ENABLE,
  output [3:0] R
);

  wire clock_1_out;
  wire [3:0] mux21_4b_1_s;

  Clock clock_1 (.out(clock_1_out));
  mux21_4b mux21_4b_1 (.A(R), .B(A), .SEL(ENABLE), .S(mux21_4b_1_s));
  registrador4bits registrador4bits_1 (.D(mux21_4b_1_s), .in_2(clock_1_out), .out_3(R));
endmodule

module latch_d (
  input  in_1,
  input  in_2,
  output out_3
);

  wire and_1_out, and_2_out, nor_1_out, not_1_out;

  not not_1 (not_1_out, in_1);
  and and_1 (and_1_out, in_1, in_2);
  and and_2 (and_2_out, in_2, not_1_out);
  nor nor_1 (nor_1_out, and_1_out, out_3);
  nor nor_2 (out_3, nor_1_out, and_2_out);
endmodule

module flip_flop_d (
  input  in_1,
  input  in_2,
  output out_3
);

  wire latch_d_1_out_3, not_1_out;

  not not_1 (not_1_out, in_2);
  latch_d latch_d_1 (.in_1(in_1), .in_2(not_1_out), .out_3(latch_d_1_out_3));
  latch_d latch_d_2 (.in_1(latch_d_1_out_3), .in_2(in_2), .out_3(out_3));
endmodule

module teste (
  input  in_1,
  input  in_2,
  input  in_3,
  output out_4,
  output out_5,
  output out_6,
  output out_7,
  output out_8,
  output out_9,
  output out_10,
  output out_11
);

  wire clock_1_out;

  Counter counter_1 ();  // open: load, D, count, Q, carry, clk, clr
  Clock clock_1 (.out(clock_1_out));
  flip_flop_d flip_flop_d_1 (.in_1(in_1), .in_2(in_2), .out_3(out_4));
  slide_flip_flop_d slide_flip_flop_d_1 (.D(in_3), .CLK(clock_1_out), .Q(out_8));
  flip_flop_d flip_flop_d_2 (.in_1(out_4), .in_2(in_2), .out_3(out_5));
  slide_flip_flop_d slide_flip_flop_d_2 (.D(out_8), .CLK(clock_1_out), .Q(out_9));
  flip_flop_d flip_flop_d_3 (.in_1(out_5), .in_2(in_2), .out_3(out_6));
  slide_flip_flop_d slide_flip_flop_d_3 (.D(out_9), .CLK(clock_1_out), .Q(out_10));
  flip_flop_d flip_flop_d_4 (.in_1(out_6), .in_2(in_2), .out_3(out_7));
  slide_flip_flop_d slide_flip_flop_d_4 (.D(out_10), .CLK(clock_1_out), .Q(out_11));
endmodule

module slide_latch_d (
  input  in_1,
  input  in_2,
  output out_3
);

  wire and_1_out, and_2_out, nor_1_out, not_1_out;

  not not_1 (not_1_out, in_1);
  and and_1 (and_1_out, in_1, in_2);
  and and_2 (and_2_out, in_2, not_1_out);
  nor nor_1 (nor_1_out, and_1_out, out_3);
  nor nor_2 (out_3, nor_1_out, and_2_out);
endmodule

module slide_flip_flop_d (
  input  D,
  input  CLK,
  output Q
);

  wire not_1_out, slide_latch_d_1_out_3;

  not not_1 (not_1_out, CLK);
  slide_latch_d slide_latch_d_1 (.in_1(D), .in_2(not_1_out), .out_3(slide_latch_d_1_out_3));
  slide_latch_d slide_latch_d_2 (.in_1(slide_latch_d_1_out_3), .in_2(CLK), .out_3(Q));

  // Notes on the sheet:
  //   master
  //   slave
endmodule

module registrador4bits (
  input  [3:0] D,
  input  in_2,
  output [3:0] out_3
);

  slide_flip_flop_d slide_flip_flop_d_1 (.D(D[3]), .CLK(in_2), .Q(out_3[3]));
  slide_flip_flop_d slide_flip_flop_d_2 (.D(D[2]), .CLK(in_2), .Q(out_3[2]));
  slide_flip_flop_d slide_flip_flop_d_3 (.D(D[1]), .CLK(in_2), .Q(out_3[1]));
  slide_flip_flop_d slide_flip_flop_d_4 (.D(D[0]), .CLK(in_2), .Q(out_3[0]));
endmodule

module mux21 (
  input  A,
  input  SEL,
  input  B,
  output Q
);

  wire and_1_out, and_2_out, not_1_out;

  not not_1 (not_1_out, SEL);
  and and_1 (and_1_out, A, not_1_out);
  and and_2 (and_2_out, SEL, B);
  or or_1 (Q, and_1_out, and_2_out);
endmodule

module mux21_4b (
  input  [3:0] A,
  input  [3:0] B,
  input  SEL,
  output [3:0] S
);

  mux21 mux21_1 (.A(A[3]), .SEL(SEL), .B(B[3]), .Q(S[3]));
  mux21 mux21_2 (.A(A[2]), .SEL(SEL), .B(B[2]), .Q(S[2]));
  mux21 mux21_3 (.A(A[1]), .SEL(SEL), .B(B[1]), .Q(S[1]));
  mux21 mux21_4 (.A(A[0]), .SEL(SEL), .B(B[0]), .Q(S[0]));
endmodule
